# Fritzing sketch huzzah_wiring (saved by Fritzing 0.9.5d)
breadboards: 1

parts:
  Composant1 = Adafruit HUZZAH32 ESP32 Feather [part_number="Adafruit #3405"]
  Composant2 = Adafruit PDM Mic [part_number="Adafruit #3492"]

nets:
  N1: Composant1.IO16, Composant2.DATA
  GND: Composant1.GND, Composant2.GND
  3.3V: Composant1.3.3V, Composant2.VDD
  N2: Composant1.IO15_A8, Composant2.CLK

custom parts:
  Adafruit PDM Mic: An exotic new microphone has arrived in the Adafruit shop, a PDM MEMS Microphone! PDM is the 'third' kind of microphone you can integrate with electronics, apart from analog or I2S. These microphones are very commonly used in products, but are rarely seen in maker projects. Still, they have some benefits so we thought we'd offer a breakout for the shop. The first thing to note is that this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
